// Logisim project ALU.circ as structural Verilog: 17 circuits, main circuit ALU
module HalfAdder (
  input  AI,
  input  BI,
  output SUM,
  output Carry
);

  xor xor_1 (SUM, AI, BI);
  and and_1 (Carry, AI, BI);
endmodule

module FullAdder (
  input  AI,
  input  BI,
  input  CI,
  output SUM,
  output CI_1
);

  wire and_1_out, and_2_out, xor_1_out;

  xor xor_1 (xor_1_out, AI, BI);
  and and_1 (and_1_out, AI, BI);
  and and_2 (and_2_out, xor_1_out, CI);
  xor xor_2 (SUM, xor_1_out, CI);
  or or_1 (CI_1, and_1_out, and_2_out);
endmodule

module _8bitAdder (
  input  a7,
  input  in_2,
  input  a6,
  input  in_4,
  input  a5,
  input  in_6,
  input  a4,
  input  in_8,
  input  a3,
  input  in_10,
  input  a2,
  input  in_12,
  input  a1,
  input  b1,
  input  a0,
  input  b0,
  output out_17,
  output out_18,
  output out_19,
  output out_20,
  output out_21,
  output out_22,
  output out_23,
  output out_24,
  output Overflow
);

  wire fulladder_1_ci_1, fulladder_2_ci_1, fulladder_3_ci_1, fulladder_4_ci_1, fulladder_5_ci_1,
       fulladder_6_ci_1, fulladder_7_ci_1, halfadder_1_carry;

  xor xor_1 (Overflow, fulladder_2_ci_1, fulladder_1_ci_1);
  FullAdder fulladder_1 (.AI(a7), .BI(in_2), .CI(fulladder_2_ci_1), .SUM(out_17), .CI_1(fulladder_1_ci_1));
  FullAdder fulladder_2 (.AI(a6), .BI(in_4), .CI(fulladder_3_ci_1), .SUM(out_18), .CI_1(fulladder_2_ci_1));
  FullAdder fulladder_3 (.AI(a5), .BI(in_6), .CI(fulladder_4_ci_1), .SUM(out_19), .CI_1(fulladder_3_ci_1));
  FullAdder fulladder_4 (.AI(a4), .BI(in_8), .CI(fulladder_5_ci_1), .SUM(out_20), .CI_1(fulladder_4_ci_1));
  FullAdder fulladder_5 (.AI(a3), .BI(in_10), .CI(fulladder_6_ci_1), .SUM(out_21), .CI_1(fulladder_5_ci_1));
  FullAdder fulladder_6 (.AI(a2), .BI(in_12), .CI(fulladder_7_ci_1), .SUM(out_22), .CI_1(fulladder_6_ci_1));
  FullAdder fulladder_7 (.AI(a1), .BI(b1), .CI(halfadder_1_carry), .SUM(out_23), .CI_1(fulladder_7_ci_1));
  HalfAdder halfadder_1 (.AI(a0), .BI(b0), .SUM(out_24), .Carry(halfadder_1_carry));
endmodule

module _8Adder (
  input  [7:0] in_1,
  input  [7:0] in_2,
  output overflow,
  output [7:0] out_4
);

  _8bitAdder u_8bitadder_1 (
    .out_24(out_4[0]), .a0(in_1[0]), .b0(in_2[0]), .a1(in_1[1]), .b1(in_2[1]), .a2(in_1[2]), .in_12(in_2[2]),
    .a3(in_1[3]), .in_10(in_2[3]), .a4(in_1[4]), .in_8(in_2[4]), .a5(in_1[5]), .in_6(in_2[5]), .a6(in_1[6]),
    .in_4(in_2[6]), .a7(in_1[7]), .in_2(in_2[7]), .out_23(out_4[1]), .out_22(out_4[2]), .out_21(out_4[3]),
    .out_20(out_4[4]), .out_19(out_4[5]), .out_18(out_4[6]), .out_17(out_4[7]), .Overflow(overflow));
endmodule

module complemento2 (
  input  [7:0] in_1,
  output [7:0] out_2
);

  wire [7:0] not_1_out;

  assign not_1_out = ~in_1;  // NOT_Gate not_1, 8 bits wide
  _8Adder u_8adder_1 (.in_1(8'h1), .in_2(not_1_out), .out_4(out_2));  // open: overflow
endmodule

module _8Subtracter (
  input  [7:0] in_1,
  input  [7:0] in_2,
  output overflow,
  output [7:0] out_4
);

  wire [7:0] complemento2_1_out_2;

  complemento2 complemento2_1 (.in_1(in_2), .out_2(complemento2_1_out_2));
  _8Adder u_8adder_1 (.in_1(in_1), .in_2(complemento2_1_out_2), .out_4(out_4));  // open: overflow
endmodule

module _8bitMultiplier (
  input  in_1,
  input  in_2,
  input  in_3,
  input  in_4,
  input  in_5,
  input  in_6,
  input  in_7,
  input  x0,
  input  y0,
  input  in_10,
  input  in_11,
  input  in_12,
  input  in_13,
  input  in_14,
  input  in_15,
  input  in_16,
  output out_17,
  output out_18,
  output out_19,
  output out_20,
  output out_21,
  output out_22,
  output out_23,
  output out_24
);

  wire and_1_out, and_2_out, and_3_out, and_4_out, and_5_out, and_6_out, and_7_out, and_8_out, and_9_out,
       and_10_out, and_11_out, and_12_out, and_13_out, and_14_out, and_15_out, and_16_out, and_17_out,
       and_18_out, and_19_out, and_20_out, and_21_out, and_22_out, and_23_out, and_24_out, and_25_out,
       and_26_out, and_27_out, and_28_out, and_29_out, and_30_out, and_31_out, and_32_out, and_33_out,
       and_34_out, and_35_out, and_36_out, and_37_out, and_38_out, and_39_out, and_40_out, and_41_out,
       and_42_out, and_43_out, and_44_out, and_45_out, and_46_out, and_47_out, and_48_out, and_49_out,
       and_50_out, and_51_out, and_52_out, and_53_out, and_54_out, and_55_out, and_56_out, and_57_out,
       and_58_out, and_59_out, and_60_out, and_61_out, and_62_out, and_63_out, fulladder_1_ci_1,
       fulladder_1_sum, fulladder_2_ci_1, fulladder_2_sum, fulladder_3_ci_1, fulladder_3_sum,
       fulladder_4_ci_1, fulladder_4_sum, fulladder_5_ci_1, fulladder_5_sum, fulladder_6_ci_1,
       fulladder_6_sum, fulladder_7_ci_1, fulladder_7_sum, fulladder_8_ci_1, fulladder_8_sum,
       fulladder_9_ci_1, fulladder_9_sum, fulladder_10_ci_1, fulladder_10_sum, fulladder_11_ci_1,
       fulladder_11_sum, fulladder_12_ci_1, fulladder_12_sum, fulladder_13_ci_1, fulladder_13_sum,
       fulladder_14_ci_1, fulladder_14_sum, fulladder_15_ci_1, fulladder_15_sum, fulladder_16_ci_1,
       fulladder_16_sum, fulladder_17_ci_1, fulladder_17_sum, fulladder_18_ci_1, fulladder_18_sum,
       fulladder_19_ci_1, fulladder_19_sum, fulladder_20_ci_1, fulladder_20_sum, fulladder_21_ci_1,
       fulladder_21_sum, fulladder_22_ci_1, fulladder_22_sum, fulladder_23_ci_1, fulladder_23_sum,
       fulladder_24_ci_1, fulladder_24_sum, fulladder_25_ci_1, fulladder_25_sum, fulladder_26_ci_1,
       fulladder_26_sum, fulladder_27_ci_1, fulladder_27_sum, fulladder_28_ci_1, fulladder_28_sum,
       fulladder_29_ci_1, fulladder_29_sum, fulladder_30_ci_1, fulladder_30_sum, fulladder_31_ci_1,
       fulladder_31_sum, fulladder_32_ci_1, fulladder_32_sum, fulladder_33_ci_1, fulladder_33_sum,
       fulladder_34_ci_1, fulladder_34_sum, fulladder_35_ci_1, fulladder_35_sum, fulladder_36_ci_1,
       fulladder_36_sum, fulladder_37_ci_1, fulladder_37_sum, fulladder_38_ci_1, fulladder_38_sum,
       fulladder_39_ci_1, fulladder_39_sum, fulladder_40_ci_1, fulladder_40_sum, fulladder_41_ci_1,
       fulladder_41_sum, fulladder_42_ci_1, fulladder_42_sum, fulladder_43_ci_1, fulladder_43_sum,
       fulladder_44_ci_1, fulladder_44_sum, fulladder_45_ci_1, fulladder_45_sum, fulladder_46_ci_1,
       fulladder_46_sum, fulladder_47_ci_1, fulladder_47_sum, fulladder_48_ci_1, fulladder_48_sum,
       fulladder_49_ci_1, fulladder_49_sum, halfadder_1_sum, halfadder_2_carry, halfadder_2_sum,
       halfadder_3_carry, halfadder_4_carry, halfadder_5_carry, halfadder_6_carry, halfadder_7_carry,
       halfadder_8_carry, not_1_out, not_2_out, not_3_out, not_4_out, not_5_out, not_6_out, not_7_out,
       not_8_out, not_9_out, not_10_out, not_11_out, not_12_out, not_13_out, not_14_out;

  HalfAdder halfadder_1 (.AI(1'b1), .BI(fulladder_1_ci_1), .SUM(halfadder_1_sum));  // open: Carry
  FullAdder fulladder_1 (
    .AI(fulladder_2_ci_1), .BI(and_1_out), .CI(fulladder_3_ci_1), .SUM(fulladder_1_sum),
    .CI_1(fulladder_1_ci_1));
  and and_1 (and_1_out, in_1, in_16);
  and and_2 (and_2_out, in_1, in_15);
  not not_1 (not_1_out, and_2_out);
  FullAdder fulladder_2 (
    .AI(fulladder_4_ci_1), .BI(not_1_out), .CI(fulladder_5_ci_1), .SUM(fulladder_2_sum),
    .CI_1(fulladder_2_ci_1));
  and and_3 (and_3_out, in_2, in_16);
  not not_2 (not_2_out, and_3_out);
  FullAdder fulladder_3 (
    .AI(fulladder_2_sum), .BI(not_2_out), .CI(fulladder_6_ci_1), .SUM(fulladder_3_sum),
    .CI_1(fulladder_3_ci_1));
  and and_4 (and_4_out, in_1, in_14);
  not not_3 (not_3_out, and_4_out);
  FullAdder fulladder_4 (
    .AI(fulladder_7_ci_1), .BI(not_3_out), .CI(fulladder_8_ci_1), .SUM(fulladder_4_sum),
    .CI_1(fulladder_4_ci_1));
  and and_5 (and_5_out, in_2, in_15);
  FullAdder fulladder_5 (
    .AI(fulladder_4_sum), .BI(and_5_out), .CI(fulladder_10_ci_1), .SUM(fulladder_5_sum),
    .CI_1(fulladder_5_ci_1));
  FullAdder fulladder_6 (
    .AI(fulladder_5_sum), .BI(not_5_out), .CI(fulladder_11_ci_1), .SUM(fulladder_6_sum),
    .CI_1(fulladder_6_ci_1));
  and and_6 (and_6_out, in_1, in_13);
  not not_4 (not_4_out, and_6_out);
  FullAdder fulladder_7 (
    .AI(fulladder_9_ci_1), .BI(not_4_out), .CI(fulladder_12_ci_1), .SUM(fulladder_7_sum),
    .CI_1(fulladder_7_ci_1));
  FullAdder fulladder_8 (
    .AI(fulladder_7_sum), .BI(and_8_out), .CI(fulladder_13_ci_1), .SUM(fulladder_8_sum),
    .CI_1(fulladder_8_ci_1));
  and and_7 (and_7_out, in_3, in_16);
  not not_5 (not_5_out, and_7_out);
  FullAdder fulladder_9 (
    .AI(fulladder_16_ci_1), .BI(not_7_out), .CI(fulladder_17_ci_1), .SUM(fulladder_9_sum),
    .CI_1(fulladder_9_ci_1));
  and and_8 (and_8_out, in_2, in_14);
  and and_9 (and_9_out, in_3, in_15);
  FullAdder fulladder_10 (
    .AI(fulladder_8_sum), .BI(and_9_out), .CI(fulladder_14_ci_1), .SUM(fulladder_10_sum),
    .CI_1(fulladder_10_ci_1));
  and and_10 (and_10_out, in_4, in_16);
  not not_6 (not_6_out, and_10_out);
  FullAdder fulladder_11 (
    .AI(fulladder_10_sum), .BI(not_6_out), .CI(fulladder_15_ci_1), .SUM(fulladder_11_sum),
    .CI_1(fulladder_11_ci_1));
  ExactlyOne xor_1 (
    .out(out_24), .in0(halfadder_1_sum), .in1(fulladder_1_sum), .in2(fulladder_3_sum), .in3(fulladder_6_sum),
    .in4(fulladder_11_sum), .in5(fulladder_15_sum), .in6(fulladder_24_sum), .in7(fulladder_29_sum),
    .in8(halfadder_2_sum));
  and and_11 (and_11_out, in_1, in_12);
  not not_7 (not_7_out, and_11_out);
  and and_12 (and_12_out, in_2, in_13);
  FullAdder fulladder_12 (
    .AI(fulladder_9_sum), .BI(and_12_out), .CI(fulladder_18_ci_1), .SUM(fulladder_12_sum),
    .CI_1(fulladder_12_ci_1));
  and and_13 (and_13_out, in_3, in_14);
  FullAdder fulladder_13 (
    .AI(fulladder_12_sum), .BI(and_13_out), .CI(fulladder_19_ci_1), .SUM(fulladder_13_sum),
    .CI_1(fulladder_13_ci_1));
  and and_14 (and_14_out, in_4, in_15);
  FullAdder fulladder_14 (
    .AI(fulladder_13_sum), .BI(and_14_out), .CI(fulladder_23_ci_1), .SUM(fulladder_14_sum),
    .CI_1(fulladder_14_ci_1));
  FullAdder fulladder_15 (
    .AI(fulladder_14_sum), .BI(not_9_out), .CI(fulladder_24_ci_1), .SUM(fulladder_15_sum),
    .CI_1(fulladder_15_ci_1));
  and and_15 (and_15_out, in_1, in_11);
  not not_8 (not_8_out, and_15_out);
  FullAdder fulladder_16 (
    .AI(fulladder_20_ci_1), .BI(not_8_out), .CI(fulladder_21_ci_1), .SUM(fulladder_16_sum),
    .CI_1(fulladder_16_ci_1));
  and and_16 (and_16_out, in_2, in_12);
  FullAdder fulladder_17 (
    .AI(fulladder_16_sum), .BI(and_16_out), .CI(fulladder_22_ci_1), .SUM(fulladder_17_sum),
    .CI_1(fulladder_17_ci_1));
  and and_17 (and_17_out, in_3, in_13);
  FullAdder fulladder_18 (
    .AI(fulladder_17_sum), .BI(and_17_out), .CI(fulladder_26_ci_1), .SUM(fulladder_18_sum),
    .CI_1(fulladder_18_ci_1));
  FullAdder fulladder_19 (
    .AI(fulladder_18_sum), .BI(and_21_out), .CI(fulladder_27_ci_1), .SUM(fulladder_19_sum),
    .CI_1(fulladder_19_ci_1));
  and and_18 (and_18_out, in_5, in_16);
  not not_9 (not_9_out, and_18_out);
  and and_19 (and_19_out, in_1, in_10);
  not not_10 (not_10_out, and_19_out);
  FullAdder fulladder_20 (
    .AI(1'b1), .BI(not_10_out), .CI(fulladder_25_ci_1), .SUM(fulladder_20_sum), .CI_1(fulladder_20_ci_1));
  and and_20 (and_20_out, in_2, in_11);
  FullAdder fulladder_21 (
    .AI(fulladder_20_sum), .BI(and_20_out), .CI(fulladder_30_ci_1), .SUM(fulladder_21_sum),
    .CI_1(fulladder_21_ci_1));
  FullAdder fulladder_22 (
    .AI(fulladder_21_sum), .BI(and_25_out), .CI(fulladder_31_ci_1), .SUM(fulladder_22_sum),
    .CI_1(fulladder_22_ci_1));
  and and_21 (and_21_out, in_4, in_14);
  and and_22 (and_22_out, in_5, in_15);
  FullAdder fulladder_23 (
    .AI(fulladder_19_sum), .BI(and_22_out), .CI(fulladder_28_ci_1), .SUM(fulladder_23_sum),
    .CI_1(fulladder_23_ci_1));
  and and_23 (and_23_out, in_14, in_16);
  not not_11 (not_11_out, and_23_out);
  FullAdder fulladder_24 (
    .AI(fulladder_23_sum), .BI(not_11_out), .CI(fulladder_29_ci_1), .SUM(fulladder_24_sum),
    .CI_1(fulladder_24_ci_1));
  and and_24 (and_24_out, in_1, y0);
  not not_12 (not_12_out, and_24_out);
  FullAdder fulladder_25 (
    .AI(not_12_out), .BI(and_29_out), .CI(fulladder_34_ci_1), .SUM(fulladder_25_sum), .CI_1(fulladder_25_ci_1));
  and and_25 (and_25_out, in_3, in_12);
  and and_26 (and_26_out, in_4, in_13);
  FullAdder fulladder_26 (
    .AI(fulladder_22_sum), .BI(and_26_out), .CI(fulladder_32_ci_1), .SUM(fulladder_26_sum),
    .CI_1(fulladder_26_ci_1));
  and and_27 (and_27_out, in_5, in_14);
  FullAdder fulladder_27 (
    .AI(fulladder_26_sum), .BI(and_27_out), .CI(fulladder_33_ci_1), .SUM(fulladder_27_sum),
    .CI_1(fulladder_27_ci_1));
  and and_28 (and_28_out, in_14, in_15);
  FullAdder fulladder_28 (
    .AI(fulladder_27_sum), .BI(and_28_out), .CI(fulladder_37_ci_1), .SUM(fulladder_28_sum),
    .CI_1(fulladder_28_ci_1));
  FullAdder fulladder_29 (
    .AI(fulladder_28_sum), .BI(not_13_out), .CI(halfadder_2_carry), .SUM(fulladder_29_sum),
    .CI_1(fulladder_29_ci_1));
  and and_29 (and_29_out, in_2, in_10);
  and and_30 (and_30_out, in_3, in_11);
  FullAdder fulladder_30 (
    .AI(fulladder_25_sum), .BI(and_30_out), .CI(fulladder_35_ci_1), .SUM(fulladder_30_sum),
    .CI_1(fulladder_30_ci_1));
  and and_31 (and_31_out, in_4, in_12);
  FullAdder fulladder_31 (
    .AI(fulladder_30_sum), .BI(and_31_out), .CI(fulladder_36_ci_1), .SUM(fulladder_31_sum),
    .CI_1(fulladder_31_ci_1));
  and and_32 (and_32_out, in_5, in_13);
  FullAdder fulladder_32 (
    .AI(fulladder_31_sum), .BI(and_32_out), .CI(fulladder_39_ci_1), .SUM(fulladder_32_sum),
    .CI_1(fulladder_32_ci_1));
  FullAdder fulladder_33 (
    .AI(fulladder_32_sum), .BI(and_37_out), .CI(fulladder_40_ci_1), .SUM(fulladder_33_sum),
    .CI_1(fulladder_33_ci_1));
  and and_33 (and_33_out, in_7, in_16);
  not not_13 (not_13_out, and_33_out);
  and and_34 (and_34_out, in_2, y0);
  and and_35 (and_35_out, in_3, in_10);
  FullAdder fulladder_34 (
    .AI(and_34_out), .BI(and_35_out), .CI(fulladder_38_ci_1), .SUM(fulladder_34_sum), .CI_1(fulladder_34_ci_1));
  and and_36 (and_36_out, in_4, in_11);
  FullAdder fulladder_35 (
    .AI(fulladder_34_sum), .BI(and_36_out), .CI(fulladder_41_ci_1), .SUM(fulladder_35_sum),
    .CI_1(fulladder_35_ci_1));
  FullAdder fulladder_36 (
    .AI(fulladder_35_sum), .BI(and_41_out), .CI(fulladder_42_ci_1), .SUM(fulladder_36_sum),
    .CI_1(fulladder_36_ci_1));
  and and_37 (and_37_out, in_6, in_14);
  and and_38 (and_38_out, in_7, in_15);
  FullAdder fulladder_37 (
    .AI(fulladder_33_sum), .BI(and_38_out), .CI(halfadder_3_carry), .SUM(fulladder_37_sum),
    .CI_1(fulladder_37_ci_1));
  and and_39 (and_39_out, x0, in_16);
  not not_14 (not_14_out, and_39_out);
  HalfAdder halfadder_2 (.AI(fulladder_37_sum), .BI(not_14_out), .SUM(halfadder_2_sum), .Carry(halfadder_2_carry));
  and and_40 (and_40_out, in_3, y0);
  FullAdder fulladder_38 (
    .AI(and_40_out), .BI(and_45_out), .CI(fulladder_44_ci_1), .SUM(fulladder_38_sum), .CI_1(fulladder_38_ci_1));
  and and_41 (and_41_out, in_5, in_12);
  and and_42 (and_42_out, in_6, in_13);
  FullAdder fulladder_39 (
    .AI(fulladder_36_sum), .BI(and_42_out), .CI(fulladder_43_ci_1), .SUM(fulladder_39_sum),
    .CI_1(fulladder_39_ci_1));
  and and_43 (and_43_out, in_7, in_14);
  FullAdder fulladder_40 (
    .AI(fulladder_39_sum), .BI(and_43_out), .CI(halfadder_4_carry), .SUM(fulladder_40_sum),
    .CI_1(fulladder_40_ci_1));
  and and_44 (and_44_out, x0, in_15);
  HalfAdder halfadder_3 (.AI(fulladder_40_sum), .BI(and_44_out), .SUM(out_17), .Carry(halfadder_3_carry));
  and and_45 (and_45_out, in_4, in_10);
  and and_46 (and_46_out, in_5, in_11);
  FullAdder fulladder_41 (
    .AI(fulladder_38_sum), .BI(and_46_out), .CI(fulladder_45_ci_1), .SUM(fulladder_41_sum),
    .CI_1(fulladder_41_ci_1));
  and and_47 (and_47_out, in_6, in_12);
  FullAdder fulladder_42 (
    .AI(fulladder_41_sum), .BI(and_47_out), .CI(fulladder_46_ci_1), .SUM(fulladder_42_sum),
    .CI_1(fulladder_42_ci_1));
  and and_48 (and_48_out, in_7, in_13);
  FullAdder fulladder_43 (
    .AI(fulladder_42_sum), .BI(and_48_out), .CI(halfadder_5_carry), .SUM(fulladder_43_sum),
    .CI_1(fulladder_43_ci_1));
  HalfAdder halfadder_4 (.AI(fulladder_43_sum), .BI(and_52_out), .SUM(out_18), .Carry(halfadder_4_carry));
  and and_49 (and_49_out, in_4, y0);
  and and_50 (and_50_out, in_5, in_10);
  FullAdder fulladder_44 (
    .AI(and_49_out), .BI(and_50_out), .CI(fulladder_47_ci_1), .SUM(fulladder_44_sum), .CI_1(fulladder_44_ci_1));
  and and_51 (and_51_out, in_6, in_11);
  FullAdder fulladder_45 (
    .AI(fulladder_44_sum), .BI(and_51_out), .CI(fulladder_48_ci_1), .SUM(fulladder_45_sum),
    .CI_1(fulladder_45_ci_1));
  FullAdder fulladder_46 (
    .AI(fulladder_45_sum), .BI(and_54_out), .CI(halfadder_6_carry), .SUM(fulladder_46_sum),
    .CI_1(fulladder_46_ci_1));
  and and_52 (and_52_out, x0, in_14);
  and and_53 (and_53_out, in_5, y0);
  FullAdder fulladder_47 (
    .AI(and_53_out), .BI(and_56_out), .CI(fulladder_49_ci_1), .SUM(fulladder_47_sum), .CI_1(fulladder_47_ci_1));
  and and_54 (and_54_out, in_7, in_12);
  and and_55 (and_55_out, x0, in_13);
  HalfAdder halfadder_5 (.AI(fulladder_46_sum), .BI(and_55_out), .SUM(out_19), .Carry(halfadder_5_carry));
  and and_56 (and_56_out, in_6, in_10);
  and and_57 (and_57_out, in_7, in_11);
  FullAdder fulladder_48 (
    .AI(fulladder_47_sum), .BI(and_57_out), .CI(halfadder_7_carry), .SUM(fulladder_48_sum),
    .CI_1(fulladder_48_ci_1));
  and and_58 (and_58_out, x0, in_12);
  HalfAdder halfadder_6 (.AI(fulladder_48_sum), .BI(and_58_out), .SUM(out_20), .Carry(halfadder_6_carry));
  and and_59 (and_59_out, in_6, y0);
  and and_60 (and_60_out, in_7, in_10);
  FullAdder fulladder_49 (
    .AI(and_59_out), .BI(and_60_out), .CI(halfadder_8_carry), .SUM(fulladder_49_sum), .CI_1(fulladder_49_ci_1));
  and and_61 (and_61_out, x0, in_11);
  HalfAdder halfadder_7 (.AI(fulladder_49_sum), .BI(and_61_out), .SUM(out_21), .Carry(halfadder_7_carry));
  and and_62 (and_62_out, in_7, y0);
  HalfAdder halfadder_8 (.AI(and_62_out), .BI(and_63_out), .SUM(out_22), .Carry(halfadder_8_carry));
  and and_63 (and_63_out, x0, in_10);
  and and_64 (out_23, x0, y0);
endmodule

module _8Multiplier (
  input  [7:0] in_1,
  input  [7:0] in_2,
  output out_3,
  output [7:0] out_4
);

  _8bitMultiplier u_8bitmultiplier_1 (
    .y0(in_2[0]), .in_10(in_2[1]), .in_11(in_2[2]), .in_12(in_2[3]), .in_13(in_2[4]), .in_14(in_2[5]),
    .in_15(in_2[6]), .in_16(in_2[7]), .in_1(in_1[7]), .in_2(in_1[6]), .in_3(in_1[5]), .in_4(in_1[4]),
    .in_5(in_1[3]), .in_6(in_1[2]), .in_7(in_1[1]), .x0(in_1[0]), .out_24(out_3), .out_17(out_4[6]),
    .out_18(out_4[5]), .out_19(out_4[4]), .out_20(out_4[3]), .out_21(out_4[2]), .out_22(out_4[1]),
    .out_23(out_4[0]));
endmodule

module initialKick (
  input  clock,
  input  in_2,
  input  clear,
  output out_4
);

  wire multiplexer_1_out, nand_1_out;

  Multiplexer multiplexer_1 (.in0(in_2), .in1(out_4), .out(multiplexer_1_out), .sel(out_4));  // open: en
  nand nand_1 (nand_1_out, clock, multiplexer_1_out);
  D_Flip_Flop d_ff_1 (.clk(clock), .D(nand_1_out), .Q(out_4), .reset(clear));  // open: Qn, preset, en
endmodule

module Greather (
  input  [7:0] in_1,
  input  [7:0] in_2,
  output out_3
);

  wire [6:0] n8subtracter_1_out_4;

  _8Subtracter u_8subtracter_1 (.in_1(in_1), .in_2(in_2), .out_4({out_3, n8subtracter_1_out_4}));  // open: overflow
endmodule

module _8bitDivisor_sequencial (
  input  [7:0] in_1,
  input  clear,
  input  clock,
  input  clear_2,
  input  clear_3,
  input  clock_2,
  input  [7:0] in_7,
  input  clear_4,
  output [7:0] out_9,
  output [7:0] out_10
);

  wire and_1_out, and_2_out, and_3_out, initialkick_1_out_4, initialkick_2_out_4, multiplexer_3_out,
       not_1_out, not_2_out, not_3_out, not_4_out;
  wire [7:0] multiplexer_1_out, multiplexer_2_out, multiplexer_4_out, multiplexer_5_out,
       n8subtracter_1_out_4, register_1_q, shifter_1_out, shifter_2_out;

  Multiplexer #(.width(8)) multiplexer_1 (
    .in0(in_7), .in1(register_1_q), .out(multiplexer_1_out), .sel(initialkick_1_out_4));  // open: en
  Register register_1 (.D(multiplexer_4_out), .en(1'b1), .Q(register_1_q), .clk(multiplexer_3_out), .clr(clear_4));
  initialKick initialkick_1 (.clock(clock_2), .in_2(1'b0), .out_4(initialkick_1_out_4), .clear(clear_4));
  Multiplexer #(.width(8)) multiplexer_2 (
    .in0(in_1), .in1(multiplexer_5_out), .out(multiplexer_2_out), .sel(initialkick_2_out_4));  // open: en
  initialKick initialkick_2 (.clock(and_1_out), .in_2(1'b0), .out_4(initialkick_2_out_4), .clear(clear_2));
  Shifter shifter_1 (.in(multiplexer_1_out), .\dist (3'b001), .out(shifter_1_out));
  not not_1 (not_1_out, multiplexer_1_out[6]);
  and and_1 (and_1_out, multiplexer_1_out[6], clock);
  not not_2 (not_2_out, clock_2);
  and and_2 (and_2_out, not_1_out, clock_2);
  not not_3 (not_3_out, initialkick_2_out_4);
  Multiplexer multiplexer_3 (.in0(clock_2), .in1(and_2_out), .out(multiplexer_3_out), .sel(not_3_out));  // open: en
  Multiplexer #(.width(8)) multiplexer_4 (
    .in0(shifter_1_out), .in1(shifter_2_out), .out(multiplexer_4_out), .sel(initialkick_2_out_4));  // open: en
  Register register_2 (.D(multiplexer_2_out), .en(1'b1), .Q(out_9), .clk(clock), .clr(clear));
  Multiplexer #(.width(8)) multiplexer_5 (
    .in0(out_9), .in1(n8subtracter_1_out_4), .out(multiplexer_5_out), .sel(not_4_out));  // open: en
  _8Subtracter u_8subtracter_1 (.in_1(out_9), .in_2(register_1_q), .out_4(n8subtracter_1_out_4));  // open: overflow
  Shifter #(.shift("lr")) shifter_2 (.in(register_1_q), .\dist (3'b001), .out(shifter_2_out));
  and and_3 (and_3_out, not_2_out, initialkick_2_out_4);
  not not_4 (not_4_out, n8subtracter_1_out_4[7]);
  Shift_Register shift_register_1 (
    .shift(1'b1), .in(not_4_out), .clk(and_3_out), .clr(clear_3), .q0(out_10[0]), .q1(out_10[1]),
    .q2(out_10[2]), .q3(out_10[3]), .q4(out_10[4]), .q5(out_10[5]), .q6(out_10[6]), .q7(out_10[7]));  // open: out, load, d0, d1, d2, d3, d4, d5, d6, d7
endmodule

module Divisor_sequecial (
  input  [7:0] dividendo,
  input  [7:0] in_2,
  input  in_3,
  input  clock,
  output [7:0] out_5,
  output [7:0] out_6
);

  wire and_1_out, greather_1_out_3, not_1_out;

  and and_1 (and_1_out, clock, not_1_out);
  not not_1 (not_1_out, greather_1_out_3);
  _8bitDivisor_sequencial u_8bitdivisor_sequencial_1 (
    .in_7(in_2), .clear_4(in_3), .in_1(dividendo), .clear(in_3), .clear_2(in_3), .out_9(out_6),
    .out_10(out_5), .clock_2(and_1_out), .clock(clock), .clear_3(in_3));
  Greather greather_1 (.in_1(out_6), .in_2(in_2), .out_3(greather_1_out_3));

  // Notes on the sheet:
  //   divisor
endmodule

module R_Adder (
  input  in_1,
  input  in_2,
  input  in_3,
  input  in_4,
  input  in_5,
  input  in_6,
  input  in_7,
  output [2:0] out_8
);

  wire [7:0] n8adder_1_out_4, n8adder_2_out_4, n8adder_3_out_4, n8adder_4_out_4, n8adder_5_out_4,
       n8adder_6_out_4;
  wire [7:3] n8adder_7_out_4;

  _8Adder u_8adder_1 (.in_1(8'h1), .in_2({{7{1'b0}}, in_1}), .out_4(n8adder_1_out_4));  // open: overflow
  _8Adder u_8adder_2 (.in_1(n8adder_1_out_4), .in_2({{7{1'b0}}, in_2}), .out_4(n8adder_2_out_4));  // open: overflow
  _8Adder u_8adder_3 (.in_1(n8adder_2_out_4), .in_2({{7{1'b0}}, in_3}), .out_4(n8adder_3_out_4));  // open: overflow
  _8Adder u_8adder_4 (.in_1(n8adder_3_out_4), .in_2({{7{1'b0}}, in_4}), .out_4(n8adder_4_out_4));  // open: overflow
  _8Adder u_8adder_5 (.in_1(n8adder_4_out_4), .in_2({{7{1'b0}}, in_5}), .out_4(n8adder_5_out_4));  // open: overflow
  _8Adder u_8adder_6 (.in_1(n8adder_5_out_4), .in_2({{7{1'b0}}, in_6}), .out_4(n8adder_6_out_4));  // open: overflow
  _8Adder u_8adder_7 (
    .in_1(n8adder_6_out_4), .in_2({{7{1'b0}}, in_7}), .out_4({n8adder_7_out_4, out_8}));  // open: overflow
endmodule

module R_Shifter (
  input  [7:0] in_1,
  output [7:0] out_2
);

  wire [0:0] not_1_out, not_2_out, not_3_out, not_4_out, not_5_out, not_6_out, not_7_out, not_8_out;
  wire [2:0] n8adder_7_out_4;
  wire [7:0] n8adder_1_out_4, n8adder_2_out_4, n8adder_3_out_4, n8adder_4_out_4, n8adder_5_out_4,
       n8adder_6_out_4, shifter_1_out, shifter_2_out, shifter_3_out, shifter_4_out, shifter_5_out,
       shifter_6_out, shifter_7_out;
  wire [7:3] n8adder_7_out_4_2;

  Shifter shifter_1 (.in(in_1), .\dist ({2'b00, not_1_out[0]}), .out(shifter_1_out));
  not not_1 (not_1_out[0], in_1[6]);
  _8Adder u_8adder_1 (
    .in_1({{7{1'b0}}, not_2_out[0]}), .in_2({{7{1'b0}}, not_1_out[0]}), .out_4(n8adder_1_out_4));  // open: overflow
  _8Adder u_8adder_2 (
    .in_1({{7{1'b0}}, not_3_out[0]}), .in_2(n8adder_1_out_4), .out_4(n8adder_2_out_4));  // open: overflow
  not not_2 (not_2_out[0], shifter_1_out[6]);
  _8Adder u_8adder_3 (
    .in_1({{7{1'b0}}, not_4_out[0]}), .in_2(n8adder_2_out_4), .out_4(n8adder_3_out_4));  // open: overflow
  _8Adder u_8adder_4 (
    .in_1({{7{1'b0}}, not_5_out[0]}), .in_2(n8adder_3_out_4), .out_4(n8adder_4_out_4));  // open: overflow
  _8Adder u_8adder_5 (
    .in_1({{7{1'b0}}, not_6_out[0]}), .in_2(n8adder_4_out_4), .out_4(n8adder_5_out_4));  // open: overflow
  _8Adder u_8adder_6 (
    .in_1({{7{1'b0}}, not_7_out[0]}), .in_2(n8adder_5_out_4), .out_4(n8adder_6_out_4));  // open: overflow
  Shifter shifter_2 (.in(shifter_1_out), .\dist ({2'b00, not_2_out[0]}), .out(shifter_2_out));
  not not_3 (not_3_out[0], shifter_2_out[6]);
  _8Adder u_8adder_7 (
    .in_1({{7{1'b0}}, not_8_out[0]}), .in_2(n8adder_6_out_4), .out_4({n8adder_7_out_4_2, n8adder_7_out_4}));  // open: overflow
  Shifter shifter_3 (.in(shifter_2_out), .\dist ({2'b00, not_3_out[0]}), .out(shifter_3_out));
  not not_4 (not_4_out[0], shifter_3_out[6]);
  Shifter shifter_4 (.in(shifter_3_out), .\dist ({2'b00, not_4_out[0]}), .out(shifter_4_out));
  not not_5 (not_5_out[0], shifter_4_out[6]);
  Shifter shifter_5 (.in(shifter_4_out), .\dist ({2'b00, not_5_out[0]}), .out(shifter_5_out));
  not not_6 (not_6_out[0], shifter_5_out[6]);
  Shifter shifter_6 (.in(shifter_5_out), .\dist ({2'b00, not_6_out[0]}), .out(shifter_6_out));
  not not_7 (not_7_out[0], shifter_6_out[6]);
  Shifter shifter_7 (.in(shifter_6_out), .\dist ({2'b00, not_7_out[0]}), .out(shifter_7_out));
  not not_8 (not_8_out[0], shifter_7_out[6]);
  Multiplexer #(.select(3), .width(8)) multiplexer_1 (
    .in0(in_1), .in1(shifter_1_out), .in2(shifter_2_out), .in3(shifter_3_out), .in4(shifter_4_out),
    .in5(shifter_5_out), .in6(shifter_6_out), .in7(shifter_7_out), .out(out_2), .sel(n8adder_7_out_4));  // open: en
endmodule

module DivisorUnity (
  input  in_1,
  input  [7:0] original,
  input  [7:0] dividendo,
  input  [7:0] divisor,
  output parou_nesse,
  output [7:0] out_6,
  output resultado,
  output [7:0] out_8
);

  wire greather_1_out_3, not_1_out;
  wire [7:0] n8subtracter_1_out_4;

  Greather greather_1 (.in_1(divisor), .in_2(original), .out_3(greather_1_out_3));
  _8Subtracter u_8subtracter_1 (.in_1(dividendo), .in_2(divisor), .out_4(n8subtracter_1_out_4));  // open: overflow
  not not_1 (not_1_out, n8subtracter_1_out_4[7]);
  Shifter #(.shift("lr")) shifter_1 (.in(divisor), .\dist (3'b001), .out(out_8));
  or or_1 (parou_nesse, in_1, greather_1_out_3);
  Multiplexer #(.width(8)) multiplexer_1 (
    .in0(dividendo), .in1(n8subtracter_1_out_4), .out(out_6), .sel(not_1_out));  // open: en
  Multiplexer multiplexer_2 (.in0(not_1_out), .in1(1'b0), .out(resultado), .sel(parou_nesse));  // open: en

  // Other names for the same wires on the sheet: se_parou_nesse = parou_nesse

  // Notes on the sheet:
  //   divisor
  //   parou no anterior?
  //   atuais
endmodule

module Divisor (
  input  [7:0] divisor,
  input  [7:0] dividendo,
  output [7:0] out_3
);

  wire divisorunity_1_parou_nesse, divisorunity_2_parou_nesse, divisorunity_3_parou_nesse,
       divisorunity_4_parou_nesse, divisorunity_5_parou_nesse, divisorunity_6_parou_nesse,
       divisorunity_7_parou_nesse;
  wire [2:0] r_adder_1_out_8;
  wire [7:0] divisorunity_1_out_6, divisorunity_1_out_8, divisorunity_2_out_6, divisorunity_2_out_8,
       divisorunity_3_out_6, divisorunity_3_out_8, divisorunity_4_out_6, divisorunity_4_out_8,
       divisorunity_5_out_6, divisorunity_5_out_8, divisorunity_6_out_6, divisorunity_6_out_8,
       divisorunity_7_out_6, divisorunity_7_out_8, divisorunity_8_resultado, r_shifter_1_out_2;

  R_Shifter r_shifter_1 (.in_1(divisor), .out_2(r_shifter_1_out_2));
  DivisorUnity divisorunity_1 (
    .in_1(1'b0), .parou_nesse(divisorunity_1_parou_nesse), .resultado(divisorunity_8_resultado[7]),
    .original(divisor), .dividendo(dividendo), .divisor(r_shifter_1_out_2), .out_6(divisorunity_1_out_6),
    .out_8(divisorunity_1_out_8));
  DivisorUnity divisorunity_2 (
    .in_1(divisorunity_1_parou_nesse), .parou_nesse(divisorunity_2_parou_nesse),
    .resultado(divisorunity_8_resultado[6]), .original(divisor), .dividendo(divisorunity_1_out_6),
    .divisor(divisorunity_1_out_8), .out_6(divisorunity_2_out_6), .out_8(divisorunity_2_out_8));
  DivisorUnity divisorunity_3 (
    .in_1(divisorunity_2_parou_nesse), .parou_nesse(divisorunity_3_parou_nesse),
    .resultado(divisorunity_8_resultado[5]), .original(divisor), .dividendo(divisorunity_2_out_6),
    .divisor(divisorunity_2_out_8), .out_6(divisorunity_3_out_6), .out_8(divisorunity_3_out_8));
  DivisorUnity divisorunity_4 (
    .in_1(divisorunity_3_parou_nesse), .parou_nesse(divisorunity_4_parou_nesse),
    .resultado(divisorunity_8_resultado[4]), .original(divisor), .dividendo(divisorunity_3_out_6),
    .divisor(divisorunity_3_out_8), .out_6(divisorunity_4_out_6), .out_8(divisorunity_4_out_8));
  DivisorUnity divisorunity_5 (
    .in_1(divisorunity_4_parou_nesse), .parou_nesse(divisorunity_5_parou_nesse),
    .resultado(divisorunity_8_resultado[3]), .original(divisor), .dividendo(divisorunity_4_out_6),
    .divisor(divisorunity_4_out_8), .out_6(divisorunity_5_out_6), .out_8(divisorunity_5_out_8));
  DivisorUnity divisorunity_6 (
    .in_1(divisorunity_5_parou_nesse), .parou_nesse(divisorunity_6_parou_nesse),
    .resultado(divisorunity_8_resultado[2]), .original(divisor), .dividendo(divisorunity_5_out_6),
    .divisor(divisorunity_5_out_8), .out_6(divisorunity_6_out_6), .out_8(divisorunity_6_out_8));
  DivisorUnity divisorunity_7 (
    .in_1(divisorunity_6_parou_nesse), .parou_nesse(divisorunity_7_parou_nesse),
    .resultado(divisorunity_8_resultado[1]), .original(divisor), .dividendo(divisorunity_6_out_6),
    .divisor(divisorunity_6_out_8), .out_6(divisorunity_7_out_6), .out_8(divisorunity_7_out_8));
  DivisorUnity divisorunity_8 (
    .in_1(divisorunity_7_parou_nesse), .resultado(divisorunity_8_resultado[0]), .original(divisor),
    .dividendo(divisorunity_7_out_6), .divisor(divisorunity_7_out_8));  // open: parou_nesse, out_6, out_8
  R_Adder r_adder_1 (
    .in_1(divisorunity_1_parou_nesse), .in_2(divisorunity_2_parou_nesse), .in_3(divisorunity_3_parou_nesse),
    .in_4(divisorunity_4_parou_nesse), .in_5(divisorunity_5_parou_nesse), .in_6(divisorunity_6_parou_nesse),
    .in_7(divisorunity_7_parou_nesse), .out_8(r_adder_1_out_8));
  Shifter #(.shift("lr")) shifter_1 (.in(divisorunity_8_resultado), .\dist (r_adder_1_out_8), .out(out_3));
endmodule

module ALU (
  input  [7:0] in_1,
  input  [7:0] in_2,
  input  in_3,
  input  [2:0] in_4,
  output out_5,
  output [7:0] out_6
);

  wire clock_1_out, n8adder_1_overflow, n8multiplier_1_out_3, n8subtracter_1_overflow;
  wire [7:0] divisor_sequecial_1_out_5, divisor_sequecial_1_out_6, n8adder_1_out_4, n8multiplier_1_out_4,
       n8subtracter_1_out_4;
  wire [15:0] demultiplexer_1_out0, demultiplexer_1_out1, demultiplexer_1_out2, demultiplexer_1_out3,
       demultiplexer_1_out4, multiplexer_1_out;

  Demultiplexer #(.select(3), .width(16)) demultiplexer_1 (
    .out0(demultiplexer_1_out0), .out1(demultiplexer_1_out1), .out2(demultiplexer_1_out2),
    .out3(demultiplexer_1_out3), .out4(demultiplexer_1_out4), .in({in_2, in_1}), .sel(in_4));  // open: out5, out6, out7, en
  Multiplexer #(.width(16)) multiplexer_1 (
    .in0(demultiplexer_1_out3), .in1(demultiplexer_1_out4), .out(multiplexer_1_out), .sel(in_4[2]));  // open: en
  Clock clock_1 (.out(clock_1_out));
  or or_1 (out_5, n8adder_1_overflow, n8subtracter_1_overflow, n8multiplier_1_out_3);
  _8Adder u_8adder_1 (
    .in_1(demultiplexer_1_out0[7:0]), .in_2(demultiplexer_1_out0[15:8]), .out_4(n8adder_1_out_4),
    .overflow(n8adder_1_overflow));
  _8Subtracter u_8subtracter_1 (
    .in_1(demultiplexer_1_out1[7:0]), .in_2(demultiplexer_1_out1[15:8]), .out_4(n8subtracter_1_out_4),
    .overflow(n8subtracter_1_overflow));
  _8Multiplier u_8multiplier_1 (
    .in_1(demultiplexer_1_out2[7:0]), .in_2(demultiplexer_1_out2[15:8]), .out_4(n8multiplier_1_out_4),
    .out_3(n8multiplier_1_out_3));
  Divisor_sequecial divisor_sequecial_1 (
    .dividendo(multiplexer_1_out[7:0]), .in_2(multiplexer_1_out[15:8]), .out_5(divisor_sequecial_1_out_5),
    .out_6(divisor_sequecial_1_out_6), .clock(clock_1_out), .in_3(in_3));
  Multiplexer #(.select(3), .width(8)) multiplexer_2 (
    .in0(n8adder_1_out_4), .in1(n8subtracter_1_out_4), .in2(n8multiplier_1_out_4),
    .in3(divisor_sequecial_1_out_5), .in4(divisor_sequecial_1_out_6), .out(out_6), .sel(in_4));  // open: in5, in6, in7, en
endmodule
